# Fritzing sketch Scheme (saved by Fritzing 0.7.12b)
breadboards: 1

parts:
  Arduino1 = Arduino  # not connected
  DHT1 = DHT11 Humitidy and Temperature Sensor
  Componente1 = Arduino MicroSD Shield
  R1 = Resistor [tolerance=±5% resistance=100k power=14 package=THT]

nets:
  VDD: DHT1.VDD, Componente1.5V, R1.Pin_1
  N1: DHT1.DATA, Componente1.CS, R1.Pin_0
  GND: DHT1.GND, Componente1.GND

custom parts:
  DHT11 Humitidy and Temperature Sensor: DHT11 Humidity and Temperature Sensor
